# Fritzing sketch fm transmitter (saved by Fritzing 1.0.1rc)
perfboards: 1

parts:
  Nano = Arduino Nano (Rev3.0)
  FM_transmitter = Si4713 Stereo FM Transmitter
  Nokia_5110_LCD_Module1 = Nokia 5110 LCD
  S1 = Momentary Switch [package=ksa_sealed_tac_switch]
  S2 = Momentary Switch [package=ksa_sealed_tac_switch]
  S3 = Momentary Switch [package=ksa_sealed_tac_switch]
  R1 = Resistor [tolerance=±5% power=0.25W resistance=1200 package=THT]
  R2 = Resistor [tolerance=±5% power=0.25W resistance=1200 package=THT]
  R3 = Resistor [tolerance=±5% power=0.25W resistance=1200 package=THT]

nets:
  GND: Nano.GND, FM_transmitter.GND, Nokia_5110_LCD_Module1.GND, R1.Pin_1, R2.Pin_1, R3.Pin_1
  N1: Nano.D2, S1.4
  N2: Nano.D3, S2.4
  N3: Nano.D4, S3.4
  N4: Nano.D7, Nokia_5110_LCD_Module1.CLK
  N5: Nano.D8, Nokia_5110_LCD_Module1.Din
  N6: Nano.D9, Nokia_5110_LCD_Module1.D/C
  N7: Nano.D10, Nokia_5110_LCD_Module1.BL
  N8: Nano.D11/MOSI, Nokia_5110_LCD_Module1.CE
  N9: Nano.D12/MISO, Nokia_5110_LCD_Module1.RST
  N10: Nano.5V, S1.1, S2.1, S3.1
  N11: Nano.A5, FM_transmitter.SCL
  N12: Nano.A4, FM_transmitter.SDA
  3V3: Nano.3V3, FM_transmitter.VIN, Nokia_5110_LCD_Module1.VCC
  N13: Nano.D13/SCK, FM_transmitter.RST
  N14: S1.3, R1.Pin_0
  N15: S2.3, R2.Pin_0
  N16: S3.3, R3.Pin_0

custom parts:
  Si4713 Stereo FM Transmitter: Yaaar! Become your very own pirate radio station with this FM radio transmitter. This breakout board, based on the best-of-class Si4713, is an all-in-one stereo audio FM transmitter that can also transmit RDS/RBDS data!
  Nokia 5110 LCD: Nokia 5110 Graphic 84*48 LCD module <Blue Version>
